// Logisim project G6_turno_quarta14h.circ as structural Verilog: 1 circuit, main circuit main
// MaqFixa16x16
module main (
  input  S1,
  input  S2,
  input  SC,
  input  SH2,
  input  SH1,
  input  INIT,
  input  MSA,
  input  Valvula_e_Motor
);

  wire CLK_out, M, multiplexer_2_out, V;
  wire [2:0] rom_2_data;
  wire [3:0] counter_1_q, counter_1_q_2, multiplexer_1_out, multiplexer_1_out_2;
  wire [7:0] register_1_q, rom_3_data;
  wire [15:0] rom_1_data;

  Register register_1 (
    .D({multiplexer_1_out_2, multiplexer_1_out}), .Q(register_1_q), .clk(CLK_out), .clr(INIT));  // open: en
  Hex_Digit_Display hex_digit_display_1 (.value(register_1_q[3:0]));  // open: dp
  Hex_Digit_Display hex_digit_display_2 (.value(register_1_q[7:4]));  // open: dp
  Hex_Digit_Display hex_digit_display_3 (.value(multiplexer_1_out_2));  // open: dp
  LED led_1 (.in(CLK_out));
  Clock CLK (.out(CLK_out));
  Hex_Digit_Display hex_digit_display_4 (.value(multiplexer_1_out));  // open: dp
  // Probe on rom_1_data
  ROM #(.dataWidth(16)) rom_1 (.addr(register_1_q), .data(rom_1_data));  // open: sel
  Multiplexer #(.width(8)) multiplexer_1 (
    .in0(rom_1_data[15:8]), .in1(rom_1_data[7:0]), .out({multiplexer_1_out_2, multiplexer_1_out}),
    .sel(multiplexer_2_out));  // open: en
  LED led_2 (.in(multiplexer_2_out));
  ROM #(.dataWidth(3)) rom_2 (.addr(register_1_q), .data(rom_2_data));  // open: sel
  Multiplexer #(.select(3), .disabled(0), .enable("false")) multiplexer_2 (
    .in0(S1), .in1(S2), .in2(SC), .in3(SH1), .in4(SH2), .in5(MSA), .in6(Valvula_e_Motor),
    .in7(counter_1_q_2[3]), .out(multiplexer_2_out), .sel(rom_2_data));
  LED led_3 (.in(rom_3_data[7]));
  LED led_4 (.in(rom_3_data[6]));
  LED led_5 (.in(rom_3_data[5]));
  ROM rom_3 (.addr(register_1_q), .data({rom_3_data[7:5], M, V, rom_3_data[2:0]}));  // open: sel
  LED ST1 (.in(rom_3_data[1]));
  LED ST2 (.in(rom_3_data[2]));
  LED ST0 (.in(rom_3_data[0]));
  LED u_V (.in(V));
  Hex_Digit_Display hex_digit_display_5 (.value(counter_1_q_2));  // open: dp
  Counter counter_1 (
    .load(1'b0), .Q({counter_1_q_2, counter_1_q}), .clk(CLK_out), .clr(rom_3_data[7]));  // open: D, count, carry
  Hex_Digit_Display hex_digit_display_6 (.value(counter_1_q));  // open: dp
  LED u_M (.in(M));

  // Notes on the sheet:
  //   EA
  //   ES
  //   TIC/TAC
  //      ES0  
  //      ES1
  //   ROM-ES
  //   CHORTA
  //   256 Estados
  //   8 Inputs
  //   7 Outputs
  //   Timer simples
  //   contents of rom_1 (hex, n*v repeats v):
  //   115 215 303 304 506 505 714 813 90e a00 b0c b0b d00 813 f00 1011 1010 1200 90e 13 90e 1600 1719 1800
  //   1719 1719
  //   ES0/ES1
  //   ROM-TST
  //   START TIMER
  //   contents of rom_2 (hex, n*v repeats v):
  //   2 3 0 7 4 0 1 5 0 3 4 0 2 5 3 4 0 2 0 5 0 0 5 0 5 5
  //   ROM-OUT
  //   Alexandre Costa a22007578
  //   João Eleutério a22007237
  //   Grupo 6
  //   contents of rom_3 (hex, n*v repeats v):
  //   0 0 88 8 8 d 8 8 1a 1a 1a 1f 1a 1a 9 9 f 9 9 d 1a 0 0 13 13 4
  //   Sensor do depósito 1
  //   Sensor do depósito 2
  //   Sensor de Chuva
  //   Horta regada
  //   Água a correr
  //   Poço sem água
  //   Tout
  //   TMO
  //   HORTA
  //   COUNTER
  //   DEPÓSITO
  //   RCO - 7 maior, 0 menor
  //   FURO
endmodule
