// Logisim project CNTR8_LD_nINC_CLR.circ as structural Verilog: 1 circuit, main circuit main
module main (
  input  [7:0] D,
  input  INC,
  input  LD,
  input  CLK,
  input  INIT,
  output [7:0] out_6
);

  wire and_1_out, not_1_out;

  not not_1 (not_1_out, LD);
  and and_1 (and_1_out, INC, not_1_out);
  Counter counter_1 (.load(LD), .D(D), .count(and_1_out), .Q(out_6), .clk(CLK), .clr(INIT));  // open: carry
endmodule
