// Logisim project FF8W.circ as structural Verilog: 1 circuit, main circuit main
module main (
  input  [7:0] D,
  input  W,
  input  CLK,
  output [7:0] Q
);

  wire [7:0] multiplexer_1_out;

  Multiplexer #(.width(8), .enable("false")) multiplexer_1 (.in0(Q), .in1(D), .out(multiplexer_1_out), .sel(W));
  Register register_1 (.D(multiplexer_1_out), .Q(Q), .clk(CLK));  // open: en, clr
endmodule
