// Logisim project REGFILE4.circ as structural Verilog: 1 circuit, main circuit main
module main (
  input  [1:0] WR,
  input  [7:0] D,
  input  in_3,
  input  [1:0] RSA,
  input  [1:0] RSB,
  output [7:0] R1,
  output [7:0] R2,
  output [7:0] R3,
  output [7:0] R1_2,
  output [7:0] R2_2
);

  wire W1, W2, W3;

  Decoder #(.select(2), .enable("false")) decoder_1 (.out1(W1), .out2(W2), .out3(W3), .sel(WR));  // open: out0
  Multiplexer #(.select(2), .width(8), .enable("false")) multiplexer_1 (
    .in0({8{1'b0}}), .in1(R1), .in2(R2), .in3(R3), .out(R2_2), .sel(RSB));
  // Probe on R1
  FF8W_main main_1 (.D(D), .W(W1), .CLK(in_3), .Q(R1));
  FF8W_main main_2 (.D(D), .W(W2), .CLK(in_3), .Q(R2));
  Multiplexer #(.select(2), .width(8), .enable("false")) multiplexer_2 (
    .in0({8{1'b0}}), .in1(R1), .in2(R2), .in3(R3), .out(R1_2), .sel(RSA));
  // Probe on R2
  // Probe on R3
  FF8W_main main_3 (.D(D), .W(W3), .CLK(in_3), .Q(R3));
endmodule
