// Logisim project uBas_FLUX.circ as structural Verilog: 2 circuits, main circuit main
module main (
  input  INPUTS,
  input  in_2,
  input  in_3,
  input  in_4,
  input  S3,
  input  S2,
  input  S1,
  input  S0
);

  wire CLK, EXEC, GNZ, GZ, I, INC, multiplexer_2_out, MUXA, PC_W, SEL, WACC, WO, z;
  wire [1:0] F, main_1_q, main_1_q_3, RSA, RSB, W;
  wire [3:0] alu8_jp_1_zero, main_1_q_2;
  wire [7:0] adder_1_out, alu8_jp_1_result, IM, main_2_out_6, main_3_q, main_4_r1, main_4_r1_2, main_4_r2,
       main_4_r2_2, main_4_r3, main_5_q, multiplexer_1_out, multiplexer_3_out, multiplexer_4_out, OPCODE;
  wire [7:1] main_6_q;

  Multiplexer #(.width(8), .enable("false")) multiplexer_1 (
    .in0(adder_1_out), .in1(IM), .out(multiplexer_1_out), .sel(multiplexer_2_out));
  // Probe on multiplexer_1_out
  // Probe on OPCODE
  Clock u_CLK (.out(CLK));
  Multiplexer #(.enable("false")) multiplexer_2 (.in0(GNZ), .in1(GZ), .out(multiplexer_2_out), .sel(z));
  // Probe on {main_1_q_3, main_1_q_2, main_1_q}
  FF8W_CLR_main main_1 (.D(multiplexer_1_out), .W(PC_W), .CLK(CLK), .Q({main_1_q_3, main_1_q_2, main_1_q}), .CLR(I));
  Button INIT (.out(I));
  CNTR8_LD_nINC_CLR_main main_2 (.D(OPCODE), .INC(INC), .LD(EXEC), .CLK(CLK), .out_6(main_2_out_6), .INIT(I));
  Hex_Digit_Display hex_digit_display_1 (.value(main_1_q_2));  // open: dp
  Hex_Digit_Display hex_digit_display_2 (.value({2'b00, main_1_q_3}));  // open: dp
  // Probe on main_2_out_6
  // Probe on adder_1_out
  Adder adder_1 (.a({main_1_q_3, main_1_q_2, main_1_q}), .b(8'h1), .out(adder_1_out));  // open: cin, cout
  // Probe on OPCODE
  ROM #(.dataWidth(16)) rom_1 (.addr({main_1_q_3, main_1_q_2, main_1_q}), .data({IM, OPCODE}));  // open: sel
  ROM #(.dataWidth(17)) rom_2 (
    .addr(main_2_out_6), .data({GNZ, GZ, EXEC, PC_W, MUXA, INC, F, SEL, WO, WACC, W, RSA, RSB}));  // open: sel
  // Probe on IM
  LED led_1 (.in(main_3_q[7]));
  // Probe on main_3_q
  FF8W_main main_3 (.D(multiplexer_4_out), .W(WO), .CLK(CLK), .Q(main_3_q));
  // Probe on multiplexer_4_out
  // Probe on main_4_r1
  LED led_2 (.in(main_3_q[3]));
  LED led_3 (.in(main_3_q[4]));
  LED led_4 (.in(main_3_q[5]));
  LED led_5 (.in(main_3_q[6]));
  // Probe on main_4_r2
  // Probe on main_4_r3
  // Probe on main_4_r1_2
  REGFILE4_main main_4 (
    .WR(W), .D(multiplexer_4_out), .in_3(CLK), .RSA(RSA), .R1_2(main_4_r1_2), .R2_2(main_4_r2_2), .RSB(RSB),
    .R1(main_4_r1), .R2(main_4_r2), .R3(main_4_r3));
  // Probe on main_4_r2_2
  LED led_6 (.in(main_3_q[2]));
  LED led_7 (.in(main_3_q[0]));
  LED led_8 (.in(main_3_q[1]));
  ALU8_JP alu8_jp_1 (
    .A(main_4_r1_2), .B(main_4_r2_2), .Result(alu8_jp_1_result), .Zero(alu8_jp_1_zero[0]),
    .Negative(alu8_jp_1_zero[1]), .Carry(alu8_jp_1_zero[2]), .Overflow(alu8_jp_1_zero[3]), .Control1(F[1]),
    .Control0(F[0]));
  // Probe on alu8_jp_1_result
  FF8W_CLR_main main_5 (.D(multiplexer_3_out), .W(WACC), .CLK(CLK), .Q(main_5_q), .CLR(I));
  Multiplexer #(.width(8), .enable("false")) multiplexer_3 (
    .in0(alu8_jp_1_result), .in1(IM), .out(multiplexer_3_out), .sel(MUXA));
  FF8W_CLR_main main_6 (.D({4'b0000, alu8_jp_1_zero}), .W(WACC), .CLK(CLK), .Q({main_6_q, z}), .CLR(I));
  // Probe on {INPUTS, in_2, in_3, in_4, S3, S2, S1, S0}
  // Probe on main_5_q
  // Probe on z
  // Probe on main_6_q[1]
  // Probe on main_6_q[2]
  // Probe on main_6_q[3]
  Multiplexer #(.width(8), .enable("false")) multiplexer_4 (
    .in0(main_5_q), .in1({INPUTS, in_2, in_3, in_4, S3, S2, S1, S0}), .out(multiplexer_4_out), .sel(SEL));

  // Notes on the sheet:
  //   OPCODE
  //   Cont/ uCódigo
  //   if ((gz and z) or (gnz and nz) )
  //   ESTADO
  //   UBAS_FLUX2021
  //   (SMF/PAS)
  //   if gnz and not z
  //   if gz and z
  //   CONTROLO
  //   MEM Programa
  //   ROM uCódigo
  //   contents of rom_1 (hex, n*v repeats v):
  //   450b 21d 425 21 130b 11d 825 c21 a0b 41d 425 21 b 1
  //   contents of rom_2 (hex, n*v repeats v):
  //   4000 0 2910 4000 2920 4000 2930 4000 2930 c70 4000 3840 880 4000 4000 2810 4000 2820 4000 2830 4000
  //   2a46 4000 2e46 4000 2c46 4000 2846 4000 3950 830 847 4000 1a800 4000 12800 4000 a800 4000 3840 4000
  //   ESTADO 0
  //   ESTADO 1
  //   ESTADO 2
  //   ESTADO 3
  //   PROGRAM TEST
  //   450b - OUT 45
  //   021d - TEST 02
  //   0425 - GOTOZ E1 (04)
  //   0021 - GOTO E0 (00)
  //   130b - OUT 13
  //   011d - TEST 01
  //   0825 - GOTOZ E2 (08)
  //   0c21 - GOTO E3 (0C)
  //   0a0b - OUT 0A
  //   041d - TEST 04
  //   0425 - GOTOZ E1 (04)
  //   0021 - GOTO E0 (00)
  //   000b - OUT 00
  //   0001 - HALT
  //     (OUT)
  //     (IN)
  //     (ES0)
  //     (ES1)
  //     (ES0)
  //     (ES1)
  //     (ES0)
  //     (ES1)
  //   OUT
  //   OUTPUTS
  //   DATA BUS
  //   ARQUITECTURA
  //   xx01 - HALT
  //   xx02 - IN R1
  //   xx04 - IN R2
  //   vv0b - OUT valor
  //   xx0f - MV R1, ACC
  //   xx11 - MV R2, ACC
  //   xx15 - ADD ACC, R1, R2
  //   xx17 - SUB ACC, R1, R2
  //   xx08 - IN ACC
  //   STATUS
  //   OPCODES/INST
  //   ACC
  //   xx1b - AND ACC, R1, R2
  //   xx10 - OR ACC, R1, R2
  //   vv1d - TEST mascara 
  //   vv21 - GOTO ender 
  //   vv23 - GOTONZ ender 
  //   vv25 - GOTOZ ender
  //   vv27 - MV ACC, valor
  //   FLAGS
endmodule

module jump4 (
  input  [7:0] A,
  input  z,
  output [7:0] Q
);

  wire [7:0] adder_1_out;

  Adder adder_1 (.a(A), .b(8'h4), .out(adder_1_out));  // open: cin, cout
  Multiplexer #(.width(8), .disabled(0)) multiplexer_1 (.in0(A), .in1(adder_1_out), .out(Q), .sel(z), .en(1'b1));
endmodule
