// Logisim project uBas_Flux_HortaCOMPLETO-PARA_ENTREGA (1).circ as structural Verilog: 2 circuits, main circuit main
module main (
  input  S1,
  input  S2,
  input  in_3,
  input  in_4,
  input  in_5,
  input  in_6
);

  wire CLK, EXEC, GNZ, GZ, I, INC, M, multiplexer_2_out, MUXA, PC_W, SEL, ST, ST0, ST1, ST2, TMO_L, TMO_S, V,
       WACC, WO, z;
  wire [1:0] F, main_1_q, main_1_q_3, RSA, RSB, W;
  wire [3:0] alu8_jp_1_zero, main_1_q_2;
  wire [6:0] counter_1_q;
  wire [6:5] main_3_q;
  wire [7:0] adder_1_out, alu8_jp_1_result, IM, main_2_out_6, main_4_r1, main_4_r1_2, main_4_r2, main_4_r2_2,
       main_4_r3, main_5_q, multiplexer_1_out, multiplexer_3_out, multiplexer_4_out, OPCODE;
  wire [7:1] main_6_q;

  Multiplexer #(.width(8), .enable("false")) multiplexer_1 (
    .in0(adder_1_out), .in1(IM), .out(multiplexer_1_out), .sel(multiplexer_2_out));
  // Probe on multiplexer_1_out
  // Probe on OPCODE
  Clock clock_1 (.out(CLK));
  Multiplexer #(.enable("false")) multiplexer_2 (.in0(GNZ), .in1(GZ), .out(multiplexer_2_out), .sel(z));
  // Probe on {main_1_q_3, main_1_q_2, main_1_q}
  FF8W_CLR_main main_1 (.D(multiplexer_1_out), .W(PC_W), .CLK(CLK), .Q({main_1_q_3, main_1_q_2, main_1_q}), .CLR(I));
  Button INIT (.out(I));
  CNTR8_LD_nINC_CLR_main main_2 (.D(OPCODE), .INC(INC), .LD(EXEC), .CLK(CLK), .out_6(main_2_out_6), .INIT(I));
  Hex_Digit_Display hex_digit_display_1 (.value({2'b00, main_1_q_3}));  // open: dp
  Hex_Digit_Display hex_digit_display_2 (.value(main_1_q_2));  // open: dp
  // Probe on main_2_out_6
  // Probe on adder_1_out
  Adder adder_1 (.a({main_1_q_3, main_1_q_2, main_1_q}), .b(8'h1), .out(adder_1_out));  // open: cin, cout
  // Probe on OPCODE
  ROM #(.dataWidth(16)) rom_1 (.addr({main_1_q_3, main_1_q_2, main_1_q}), .data({IM, OPCODE}));  // open: sel
  ROM #(.dataWidth(17)) rom_2 (
    .addr(main_2_out_6), .data({GNZ, GZ, EXEC, PC_W, MUXA, INC, F, SEL, WO, WACC, W, RSA, RSB}));  // open: sel
  // Probe on IM
  Counter counter_1 (
    .Q({TMO_L, counter_1_q[6:3], TMO_S, counter_1_q[1:0]}), .clk(PC_W), .clr(ST));  // open: load, D, count, carry
  LED led_1 (.in(ST));
  // Probe on {ST, main_3_q, M, V, ST2, ST1, ST0}
  FF8W_CLR_main main_3 (.D(multiplexer_4_out), .W(WO), .CLK(CLK), .Q({ST, main_3_q, M, V, ST2, ST1, ST0}), .CLR(I));
  // Probe on multiplexer_4_out
  // Probe on main_4_r1
  // Probe on main_4_r2
  // Probe on main_4_r3
  // Probe on main_4_r1_2
  REGFILE4_main main_4 (
    .WR(W), .D(multiplexer_4_out), .in_3(CLK), .RSA(RSA), .R1_2(main_4_r1_2), .R2_2(main_4_r2_2), .RSB(RSB),
    .R1(main_4_r1), .R2(main_4_r2), .R3(main_4_r3));
  // Probe on main_4_r2_2
  ALU8_JP alu8_jp_1 (
    .A(main_4_r1_2), .B(main_4_r2_2), .Result(alu8_jp_1_result), .Zero(alu8_jp_1_zero[0]),
    .Negative(alu8_jp_1_zero[1]), .Carry(alu8_jp_1_zero[2]), .Overflow(alu8_jp_1_zero[3]), .Control1(F[1]),
    .Control0(F[0]));
  // Probe on alu8_jp_1_result
  // Probe on {TMO_S, TMO_L, in_4, in_5, in_6, in_3, S2, S1}
  FF8W_CLR_main main_5 (.D(multiplexer_3_out), .W(WACC), .CLK(CLK), .Q(main_5_q), .CLR(I));
  Multiplexer #(.width(8), .enable("false")) multiplexer_3 (
    .in0(alu8_jp_1_result), .in1(IM), .out(multiplexer_3_out), .sel(MUXA));
  FF8W_CLR_main main_6 (.D({4'b0000, alu8_jp_1_zero}), .W(WACC), .CLK(CLK), .Q({main_6_q, z}), .CLR(I));
  // Probe on main_5_q
  // Probe on z
  // Probe on main_6_q[1]
  // Probe on main_6_q[2]
  // Probe on main_6_q[3]
  Multiplexer #(.width(8), .enable("false")) multiplexer_4 (
    .in0(main_5_q), .in1({TMO_S, TMO_L, in_4, in_5, in_6, in_3, S2, S1}), .out(multiplexer_4_out), .sel(SEL));
  LED led_2 (.in(V));
  LED led_3 (.in(M));
  LED led_4 (.in(ST2));
  LED led_5 (.in(ST0));
  LED led_6 (.in(ST1));

  // Other names for the same wires on the sheet: SC = in_3; SH1 = in_6; SH2 = in_5; MSA = in_4

  // Notes on the sheet:
  //   OPCODE
  //   Cont/ uCódigo
  //   if ((gz and z) or (gnz and nz) )
  //   ESTADO
  //   Grupo 2 (Quarta-Feira -> Turno das 14H)
  //   - Ricardo Cleto | Nº:(a22006526)
  //   - Rodrigo Amaro | Nº:(a22004525)
  //   UBAS_CHORTA2021
  //   (SMF/PAS)
  //   if gnz and not z
  //   if gz and z
  //   CONTROLO
  //   MEM Programa
  //   ROM uCódigo
  //   contents of rom_1 (hex, n*v repeats v):
  //   b 41d 425 23 b 81d c25 823 60b 1 0 0 100b 21d 1025 2423 130b 5821 0 0 130b 21d 1825 2423 130b 201d
  //   1c25 2023 70b 1 0 0 40b 1 0 0 100b 11d 2825 3c23 80b 2c21 0 0 80b 9021 0 0 80b 101d 3425 3823 50b 1
  //   0 0 120b 81d 3825 5423 10b 4021 0 0 80b 7821 0 0 90b 101d 4825 4c23 50b 1 0 0 90b 81d 4c25 5023 b 21
  //   0 0 b 21 0 0 12b 802e 15 11 5a23 1421 26*0 12b 802e 15 11 7a23 4421 18*0 12b 802e 15 11 9223 3021
  //   contents of rom_2 (hex, n*v repeats v):
  //   4000 0 2910 4000 2920 4000 2930 4000 2930 c70 4000 3840 880 4000 4000 2810 4000 2820 4000 2830 4000
  //   2a46 4000 2e46 4000 2c46 4000 2846 4000 3950 830 847 4000 1a800 4000 12800 4000 a800 4000 3840 4000
  //   2880 4000 3840 810 4000 3840 820 4000
  //   INPUTS:
  //   OUTPUTS:
  //   TIMER
  //   Short
  //   Long
  //   Start TIMER
  //   OUT
  //   S1 ; S2 ; SC ; SH1 ; SH2 ; MSA ; TMO_L ; TMO_S
  //   ST (Timer) ; M ; V ; ST2 ; ST1 ; ST0
  //   OUTPUTS
  //   DATA BUS
  //   ARQUITECTURA
  //   INPUTS
  //   xx01 - HALT
  //   xx02 - IN R1
  //   xx04 - IN R2
  //   vv0b - OUT valor
  //   xx0f - MV R1, ACC
  //   xx11 - MV R2, ACC
  //   xx15 - ADD ACC, R1, R2
  //   xx17 - SUB ACC, R1, R2
  //   xx08 - IN ACC *
  //   STATUS
  //   OPCODES/INST
  //   ACC
  //   xx1b - AND ACC, R1, R2
  //   xx10 - OR ACC, R1, R2
  //   vv1d - TEST mascara 
  //   vv21 - GOTO ender 
  //   vv23 - GOTONZ ender 
  //   vv25 - GOTOZ ender
  //   vv27 - MV ACC, valor
  //   xx29 - OUT ACC
  //   vv2b - MV R1, valor
  //   vv2e - MV R2, valor
  //   FLAGS
  //   Depósito
  //   HORTA
endmodule

module jump4 (
  input  [7:0] A,
  input  z,
  output [7:0] Q
);

  wire [7:0] adder_1_out;

  Adder adder_1 (.a(A), .b(8'h4), .out(adder_1_out));  // open: cin, cout
  Multiplexer #(.width(8), .disabled(0)) multiplexer_1 (.in0(A), .in1(adder_1_out), .out(Q), .sel(z), .en(1'b1));
endmodule
